# Fritzing sketch Theremax_Ultra_Lite_Lab_Edition (saved by Fritzing 0.7.12b)
breadboards: 1

parts:
  Arduino1 = Arduino
  R1 = Rotary Potentiometer (Small) [maximum_resistance=100kΩ]
  LED1 = RGB LED (com. anode, rbg) [package="5 mm [THT]"]
  R2 = Resistor [tolerance=±5% resistance=220 package=THT]
  R3 = Resistor [tolerance=±5% resistance=220 package=THT]
  R4 = Resistor [tolerance=±5% resistance=220 package=THT]

nets:
  N1: Arduino1.D11, R4.Pin_1
  N2: Arduino1.D10, R3.Pin_1
  N3: Arduino1.D9, R2.Pin_1
  N4: Arduino1.+5V, R1.leg1, LED1.common_anode
  N5: Arduino1.GND, R1.leg2
  N6: Arduino1.A0, R1.wiper
  N7: LED1.red_cathode, R4.Pin_0
  N8: LED1.blue_cathode, R3.Pin_0
  N9: LED1.green_cathode, R2.Pin_0
